# Fritzing sketch indoor_pcb (saved by Fritzing 0.8.7b)
circuit board: 8.46667cm x 5.64444cm
breadboards: 1

parts:
  U1 = atmega168 [package=dip]
  XTAL1 = Crystal [frequency="16 Mhz" package=THT]
  C3 = Ceramic Capacitor [capacitance=100nF package="100 mil [THT, multilayer]"]
  C4 = Ceramic Capacitor [capacitance=100nF package="100 mil [THT, multilayer]"]
  R1 = Resistor [tolerance=±5% resistance=10k package=THT]
  Q4 = NPN-Transistor [package="TO92 [THT]"]
  K4 = Relay [part_number=FRS1B-S package=THT]
  D4 = Rectifier Diode [part_number=1N4001 package="300 mil [THT]"]
  J2 = Screw terminal - 2 pins [package=THT]
  R2 = Resistor [tolerance=±5% resistance=10k package=THT]
  Q5 = NPN-Transistor [package="TO92 [THT]"]
  K5 = Relay [part_number=FRS1B-S package=THT]
  D5 = Rectifier Diode [part_number=1N4001 package="300 mil [THT]"]
  J3 = Screw terminal - 2 pins [package=THT]
  R3 = Resistor [tolerance=±5% resistance=10k package=THT]
  R4 = Resistor [tolerance=±5% resistance=10k package=THT]
  R7 = Photocell (LDR) [package=THT]

nets:
  N1: U1.D3_(PWM), R2.Pin_0
  N2: U1.D4, R1.Pin_0
  N3: U1.VCC, U1.AVCC, J2.pin2, J3.pin2, R7.pin_0
  GND: U1.GND, C3.1, C4.0, J2.pin1
  N4: U1.XLAT1, XTAL1.pin_0, C3.0
  N5: U1.XLAT2, XTAL1.pin_1, C4.1
  N6: U1.A0, R4.Pin_0, R7.pin_1
  N7: U1.A5, J3.pin1, R3.Pin_0
  N8: R1.Pin_1, Q4.B
  N9: Q4.C, K4.COIL1, D4.anode
  5V: K4.COIL2, D4.cathode
  N10: R2.Pin_1, Q5.B
  N11: Q5.C, K5.COIL1, D5.anode
  N12: K5.COIL2, D5.cathode
  N13: R3.Pin_1, R4.Pin_1
