# Fritzing sketch indoorpcb (saved by Fritzing 0.8.7b)
breadboards: 1

parts:
  R1 = Photocell (LDR) [package=THT]
  U1 = atmega168 [package=dip]
  XTAL1 = Crystal [frequency="16 Mhz" package=THT]
  C1 = Ceramic Capacitor [capacitance=100nF package="100 mil [THT, multilayer]"]
  C2 = Ceramic Capacitor [capacitance=100nF package="100 mil [THT, multilayer]"]
  J1 = Screw terminal - 2 pins [package=THT]
  R3 = Resistor [tolerance=±5% resistance=10k package=THT]
  K1 = Relay [part_number=FRS1B-S package=THT]
  Q1 = NPN-Transistor [package="TO92 [THT]"]
  R4 = Resistor [tolerance=±20% resistance=10k package=THT]
  D1 = Rectifier Diode [part_number=1N4001 package="300 mil [THT]"]
  K2 = Relay [part_number=FRS1B-S package=THT]
  Q2 = NPN-Transistor [package="TO92 [THT]"]
  R5 = Resistor [tolerance=±5% resistance=10k package=THT]
  D2 = Rectifier Diode [part_number=1N4001 package="300 mil [THT]"]
  R2 = Resistor [tolerance=±5% resistance=10k package=THT]

nets:
  5V: R1.pin_0, U1.VCC, U1.AVCC, J1.pin1, K1.COIL2, D1.cathode, K2.COIL2, D2.cathode
  N1: R1.pin_1, U1.A0, R2.Pin_0
  N2: U1.D2, R4.Pin_0
  N3: U1.D4, R5.Pin_0
  GND: U1.GND, C1.0, C2.1, Q1.E, Q2.E
  N4: U1.XLAT1, XTAL1.pin_1, C2.0
  N5: U1.XLAT2, XTAL1.pin_0, C1.1
  N6: U1.A1, J1.pin2, R3.Pin_1
  N7: R3.Pin_0, R2.Pin_1
  N8: K1.COIL1, Q1.C, D1.anode
  N9: Q1.B, R4.Pin_1
  N10: K2.COIL1, Q2.C, D2.anode
  N11: Q2.B, R5.Pin_1
